# Fritzing sketch rpm_computer_side (saved by Fritzing 0.8.3b)
circuit board: 5.04017cm x 2.22687cm
breadboards: 1

parts:
  CON_PC = RJ45-TRXCOM [part_number=TRJ0011BANL]
  SW = female pin header, 2 pins [form="♀ (female)"]
  LED = female pin header, 3 pins [form="♀ (female)"]
  J3 = female pin header, 4 pins [form="♀ (female)"]
  Q1 = Basic FET N-Channel [package="TO220 [THT]"]
  R1 = 10k Ω Resistor [package=THT]

nets:
  N1: CON_PC.Transmit_TD-, LED.pin1
  N2: CON_PC.Receive_RD+, LED.pin3
  N3: CON_PC.Receive_CT, SW.pin1
  N4: CON_PC.Receive_RD-, SW.pin2
  N5: CON_PC.n.c., J3.pin1
  N6: CON_PC.CHS_Ground, Q1.gate, R1.Pin_0
  N7: J3.pin2, Q1.drain
  N8: J3.pin3, Q1.source
  N9: J3.pin4, R1.Pin_1

notes:
  Power SW
  Power LED
  ATX PWR
  0V SW PWR
  +5V SW PWR
  LED+
  LED-
  Ground
  Green+
  Green-
  Violet (+5V)
