# Fritzing sketch rpm_uc_side (saved by Fritzing 0.7.12b)
breadboards: 1

parts:
  U1 = Optocoupler [package=THT]
  U2 = Optocoupler [package=THT]
  U3 = Optocoupler [package=THT]
  R1 = 1.5k Ω Resistor [package=THT]
  R2 = 1.5k Ω Resistor [package=THT]
  R3 = 1.5k Ω Resistor [package=THT]
  TRXCOM1 = RJ45-TRXCOM [part_number=TRJ0011BANL]
  J1 = female pin header, 5 pins [form="♀ (female)"]
  R4 = 10k Ω Resistor [package=THT]

nets:
  N1: U1.Pin_1, R1.Pin_0
  N2: U1.Pin_2, U2.Pin_2, U3.Pin_4, J1.pin4
  N3: U1.Pin_4, TRXCOM1.Receive_CT
  N4: U1.Pin_5, TRXCOM1.Receive_RD-
  N5: U2.Pin_1, R2.Pin_0
  N6: U2.Pin_4, TRXCOM1.n.c.
  N7: U2.Pin_5, TRXCOM1.CHS_Ground
  N8: U3.Pin_1, R3.Pin_1
  N9: U3.Pin_2, TRXCOM1.Transmit_TD-
  N10: U3.Pin_5, J1.pin2, R4.Pin_0
  N11: R1.Pin_1, J1.pin3
  N12: R2.Pin_1, J1.pin5
  N13: R3.Pin_0, TRXCOM1.Receive_RD+
  N14: J1.pin1, R4.Pin_1

notes:
  Power Switch
  ATX Power Switch
  Power LED
  pwr sw GPIO, 3.3V
  atx pwr GPIO, 3.3V, reversed
  µc ground
  Pwr LED
  µc's +3.3V
  +3.3V
  Power SW
  GND
  ATX Power
  ATX PWR
  PWR SW
